# Fritzing sketch Multicast (saved by Fritzing 0.9.2b)
breadboards: 1

parts:
  Part1 = Photon
  U1 = POT [package=pot_mammoth]

nets:
  N1: Part1.A0, U1.pin_2
  N2: Part1.GND, U1.pin_1
  N3: Part1.3V3, U1.pin_3
